# Fritzing sketch freemcom (saved by Fritzing 0.9.1b)
breadboards: 1

parts:
  arduino = Arduino Uno (Rev3)
  XBee = XBee
  Reset = Pushbutton [package=THT]
  Start/Stop = Pushbutton [package=THT]
  R1 = Resistor [tolerance=±5% resistance=10k package=THT]
  Fuse1 = Fuse with Handler [part_number=10A]
  R2 = Resistor [tolerance=±5% resistance=10k package=THT]
  J2 = Relay [part_number=SLD01101P package=THT]
  J1 = Relay [part_number=SLD01101P package=THT]
  Buzzer(12V) = Piezo Speaker
  LED1_(for_12V) = LED - 5mm [color="Red (633nm)" package="5 mm [THT]"]
  S1 = Toggle Switch [package=THT]
  R3 = Resistor [tolerance=±5% resistance=10k package=THT]
  S2 = Toggle Switch [package=THT]
  R4 = Resistor [tolerance=±5% resistance=10k package=THT]
  S3 = Toggle Switch [package=THT]

nets:
  N1: arduino.D8, R4.Pin_0, S3.L2
  N2: arduino.D9_PWM, R3.Pin_0, S2.L2
  N3: arduino.D10_PWM/SS, R2.Pin_0, S1.L2
  GND: arduino.GND, XBee.GND, Reset.leg0, R1.Pin_1, R2.Pin_1, J2.COIL2, J1.COIL2, Buzzer(12V).pin2, LED1_(for_12V).cathode, R3.Pin_1, R4.Pin_1
  N4: arduino.D0/RX, XBee.pin2
  N5: arduino.D1/TX, XBee.pin3
  N6: arduino.D2, Start/Stop.leg0, R1.Pin_0
  N7: arduino.D6_PWM, J2.COIL1
  N8: arduino.D7, J1.COIL1
  N9: arduino.RESET, Reset.leg1
  3V3: arduino.3V3, XBee.VCC
  5V: arduino.5V, arduino.VIN, Start/Stop.leg1, S1.COM, S2.COM, S3.COM
  12V: Fuse1.Connector1
  N10: Fuse1.Connector2, J2.A, J1.A
  N11: J2.C1, J2.C2, LED1_(for_12V).anode
  N12: J1.C1, J1.C2, Buzzer(12V).pin1

notes:
  NO2
  NO1
  COM2
  COM1
