# Fritzing sketch freemcom_concept (saved by Fritzing 0.8.5b)
breadboards: 1

parts:
  パーツ1 = Arduino Uno (Rev3)
  S1 = Pushbutton [package="[THT]"]
  R1 = Resistor [tolerance=±5% resistance=10k package=THT]
  LED1 = LED - 5mm [color="Red (633nm)" package="5 mm [THT]"]
  J1 = Piezo Speaker

nets:
  N1: パーツ1.D2, パーツ1.5V, S1.Pin_1, S1.Pin_2, S1.Pin_3, S1.Pin_4, R1.Pin_0
  N2: パーツ1.D4, J1.pin2
  N3: パーツ1.D5_PWM, LED1.anode
  N4: パーツ1.GND, R1.Pin_1, LED1.cathode, J1.pin1
